# Fritzing sketch arduino-lcd (saved by Fritzing 0.9.3b)
breadboards: 1

parts:
  元件1 = Arduino Mega 2560 (Rev3)
  LCD1 = LCD screen
  U1 = POT [package=3362u]

nets:
  N1: 元件1.D11_PWM, LCD1.RS
  N2: 元件1.D10_PWM, LCD1.E
  5V: 元件1.5V, LCD1.VDD, LCD1.LED+, U1.A
  GND: 元件1.GND, LCD1.VSS, LCD1.R/W, LCD1.LED-, U1.E
  N3: 元件1.D2_PWM, LCD1.DB7
  N4: 元件1.D3_PWM, LCD1.DB6
  N5: 元件1.D4_PWM, LCD1.DB5
  N6: 元件1.D5_PWM, LCD1.DB4
  N7: LCD1.V0, U1.S
