# Fritzing sketch arduino-led (saved by Fritzing 0.9.3b)

parts:
  元件6 = Arduino Mega 2560 (Rev3)
  元件5 = ws2812b [package=THT]
  元件2 = ws2812b [package=THT]
  元件4 = ws2812b [package=THT]
  元件1 = ws2812b [package=THT]
  元件7 = ws2812b [package=THT]
  元件3 = ws2812b [package=THT]

nets:
  5V: 元件6.5V, 元件1.VDD
  GND: 元件6.GND, 元件1.VSS
  N1: 元件6.D2_PWM, 元件7.DIN
  N2: 元件5.DOUT, 元件4.DIN
  N3: 元件5.DIN, 元件7.DOUT
  N4: 元件2.DOUT, 元件1.DIN
  N5: 元件2.DIN, 元件3.DOUT
  N6: 元件4.DOUT, 元件3.DIN
