# Fritzing sketch microphone (saved by Fritzing 0.9.3b)
breadboards: 1

parts:
  U1 = LM 358 Dual Op-Amp [package="SO 08 [SMD]"]  # not connected
  U2 = POT [package=trim_pot]
  U3 = POT [package=trim_pot]
  U4 = MIC [package=mic_electret_smd]

nets:
  N1: U2.A, U4.1
  N2: U3.A, U4.2
