# Fritzing sketch system (saved by Fritzing 0.9.3b)
breadboards: 2

parts:
  U1 = LM 358 Dual Op-Amp [package="SO 08 [SMD]"]  # not connected
  U2 = POT [package=trim_pot]
  U3 = POT [package=trim_pot]
  U4 = MIC [package=mic_electret_smd]
  元件1 = Arduino Mega 2560 (Rev3)
  LCD2 = LCD screen
  U5 = POT [package=3362u]
  元件8 = ws2812b [package=THT]
  元件9 = ws2812b [package=THT]
  元件10 = ws2812b [package=THT]
  元件11 = ws2812b [package=THT]
  元件12 = ws2812b [package=THT]
  元件13 = ws2812b [package=THT]

nets:
  N1: U2.A, U4.1
  VDD: U3.S, 元件1.5V, LCD2.VDD, LCD2.LED+, U5.A, 元件13.VDD
  VSS: U3.A, U4.2, 元件1.GND, LCD2.VSS, LCD2.R/W, LCD2.LED-, U5.E, 元件13.VSS
  N2: 元件1.D10_PWM, LCD2.E
  N3: 元件1.D2_PWM, LCD2.DB7, 元件8.DIN
  N4: 元件1.D3_PWM, LCD2.DB6
  N5: 元件1.D4_PWM, LCD2.DB5
  N6: 元件1.D5_PWM, LCD2.DB4
  N7: LCD2.V0, U5.S
  N8: 元件8.DOUT, 元件9.DIN
  N9: 元件9.DOUT, 元件10.DIN
  N10: 元件10.DOUT, 元件11.DIN
  N11: 元件11.DOUT, 元件12.DIN
  N12: 元件12.DOUT, 元件13.DIN
